// Logisim project circuit6.circ as structural Verilog: 1 circuit, main circuit main
module main (
  input  i1,
  input  i2,
  output out_3
);

  wire and_1_out, and_2_out, not_1_out, not_2_out, or_1_out;

  and and_1 (and_1_out, i1, i2);
  not not_1 (not_1_out, i2);
  and and_2 (and_2_out, not_1_out, i1);
  not not_2 (not_2_out, i2);
  or or_1 (or_1_out, and_1_out, and_2_out);
  or or_2 (out_3, or_1_out, not_2_out);

  // Notes on the sheet:
  //   Custom gate
endmodule
